# Fritzing sketch The_IoTeam_Circuit_Diagram (saved by Fritzing 1.0.5)
breadboards: 1

parts:
  Raspberry_Pi_1 = Raspberry Pi 3 [part_number=RPI-3-V1.2]  # not connected
  YwRobot_Power_Supply1 = YwRobot Breadboard Power Supply [part_number=545043]
  Adafruit_T-Cobbler_Plus = Adafruit T-Cobbler Plus [part_number="Adafruit #1989 and #2028"]
  Mini_Water_Pump = water pump/motor
  KY-015 = KY-015 Temperature & Humidity Sensor Module [package="Breakout board"]
  5v_DC_Fan = Fan - Ventilador [package=THT]
  16/2_LCD_Display = LCD-16X2 [package=lcd-16x2_noholes]
  part = LCM1602 IIC [part_number="LCM1602 IIC" chip_label="LCM1602 IIC" package="DIP (Dual Inline) [THT]"]
  2_channel_Relay = 2-Channel 5v Relay Shield [package=relay-2ch5v10a]
  Barometer-BMP180_Module = BMP180
  Photoresistor_Module = Grove Light Sensor
  PCF8591 = Adafruit PCF8591 [part_number="Adafruit #4648"]
  Capacitive_Soil_Moisture_Sensor1 = DFRobot Capacitive Soil Moisture Sensor V1.0 [part_number=SEN0193]
  Lm2596_DC_to_DC_Step_Down_Converter = LM2596 step down module

nets:
  VCC: YwRobot_Power_Supply1.VCC#5, YwRobot_Power_Supply1.VCC#6, part.VCC, 2_channel_Relay.Pin_5, 2_channel_Relay.Pin_13, Capacitive_Soil_Moisture_Sensor1.VCC, Lm2596_DC_to_DC_Step_Down_Converter.IN+
  VCC_2: YwRobot_Power_Supply1.VCC#9, YwRobot_Power_Supply1.VCC#10, KY-015.Vin, Barometer-BMP180_Module.3Vo, Photoresistor_Module.VCC, PCF8591.VCC
  GND: YwRobot_Power_Supply1.GND, Adafruit_T-Cobbler_Plus.GND, Mini_Water_Pump.pin_1, KY-015.-, 5v_DC_Fan.GND, part.GND, 2_channel_Relay.Pin_10, Barometer-BMP180_Module.GND, Photoresistor_Module.GND, PCF8591.GND, Capacitive_Soil_Moisture_Sensor1.GND, Lm2596_DC_to_DC_Step_Down_Converter.IN-, Lm2596_DC_to_DC_Step_Down_Converter.OUT-
  N1: Adafruit_T-Cobbler_Plus.SDA, part.SDA, Barometer-BMP180_Module.SDA, PCF8591.SDA
  N2: Adafruit_T-Cobbler_Plus.SCL, part.SCL, Barometer-BMP180_Module.SCL, PCF8591.SCL
  N3: Adafruit_T-Cobbler_Plus.GPIO17, KY-015.S
  N4: Adafruit_T-Cobbler_Plus.GPIO18, Capacitive_Soil_Moisture_Sensor1.A
  N5: Adafruit_T-Cobbler_Plus.GPIO23, 2_channel_Relay.Pin_11
  N6: Adafruit_T-Cobbler_Plus.GPIO24, 2_channel_Relay.Pin_12
  N7: Mini_Water_Pump.pin_2, 2_channel_Relay.Pin_1
  N8: 5v_DC_Fan.5V, 2_channel_Relay.Pin_4
  VSS: 16/2_LCD_Display.VSS, part.VSS
  VDD: 16/2_LCD_Display.VDD, part.VDD
  N9: 16/2_LCD_Display.VO, part.V0
  N10: 16/2_LCD_Display.RS, part.RS
  N11: 16/2_LCD_Display.R_W, part.RW
  N12: 16/2_LCD_Display.E, part.E
  N13: 16/2_LCD_Display.DB0, part.D0
  N14: 16/2_LCD_Display.DB1, part.D1
  N15: 16/2_LCD_Display.DB2, part.D2
  N16: 16/2_LCD_Display.DB3, part.D3
  N17: 16/2_LCD_Display.DB4, part.D4
  N18: 16/2_LCD_Display.DB5, part.D5
  N19: 16/2_LCD_Display.DB6, part.D6
  N20: 16/2_LCD_Display.DB7, part.D7
  N21: 16/2_LCD_Display.A, part.A
  N22: 16/2_LCD_Display.K, part.K
  N23: 2_channel_Relay.Pin_2, Lm2596_DC_to_DC_Step_Down_Converter.OUT+
  N24: Photoresistor_Module.SIG, PCF8591.AIN0

custom parts:
  YwRobot Breadboard Power Supply: The YwRobot Breadboard Power Supply (MB-V2) has two power rails; they can be 5V or 3V3. Power to the module can be provided through the female USB socket or through the A10 (female) 2.1mm power jack.
  Adafruit T-Cobbler Plus: The Raspberry Pi has landed on the Maker World like a 40-GPIO pinned, quad-USB ported, credit card sized bomb of DIY joy. And while you can use most of our great Model B accessories by hooking up our downgrade cable, its probably a good time to upgrade your set up and accessorize using all of the 40 pins. That's why we now carry the Assembled Adafruit Pi T-Cobbler Plus - Breakout + Cable for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
  water pump/motor: WATER PUMP BY ARDUBLOCKTR
  KY-015 Temperature & Humidity Sensor Module: KY-015 temperature and humidity sensor module, provides a low-latency serial interface to measure humidity and temperature.
  Fan - Ventilador: Ventilador de 2 pines, se encuentra comunmente en computadoras de escritorio
  LCM1602 IIC: I2C-Module to use a 1602 or 2004 LCD on with the wire.h libory Serial LCD Modul
  2-Channel 5v Relay Shield: 2 Channel 5v Relay Shield w. 2x SPD-06VDC-SD-C
  Adafruit PCF8591: Measuring voltage and adjusting it is what electronics is all about so you won’t get far without friends like the PCF8591 ADC+DAC combo. Analog to Digital Converters help by measuring an analog voltage and turning it into something a microcontroller like a Metro or Arduino can understand. If you’re using a single board computer like a Raspberry Pi, you might not have any other way to measure a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
  DFRobot Capacitive Soil Moisture Sensor V1.0: DFRobot Capacitive Soil Moisture Sensor V1.0 This product measures soil moisture levels by capacitive sensing, rather than resistive sensing like other types of moisture sensor. It is made of a corrosion resistant material giving it a long service life. Insert it into soil and impress your friends with the real-time soil moisture data! The product includes an on-board voltage regulator which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
  LM2596 step down module: LM2596 DC-DC step down power supply module 3 A.
